# Fritzing sketch ceng317_keypad (saved by Fritzing 0.9.3b)
circuit board: 12.7884cm x 8.56845cm
breadboards: 1

parts:
  M1 = STM32F103C8T6 blue mini board
  KEYPAD1 = Membrane Matrix Keypad

nets:
  N1: M1.A8, M1.A12, KEYPAD1.6
  N2: M1.A9, M1.B3, M1.B6, KEYPAD1.1, KEYPAD1.4
  N3: M1.A10, M1.A15, M1.B4, M1.B5, KEYPAD1.2, KEYPAD1.3, KEYPAD1.5
  N4: M1.A11, M1.B10, KEYPAD1.7

custom parts:
  Membrane Matrix Keypad: Membrane Matrix 3x4 Keypad
